// Logisim project bit32.circ as structural Verilog: 2 circuits, main circuit main
module main (
);

  wire ALU, and_1_out, and_2_out, and_3_out, and_4_out, and_5_out, and_6_out, and_7_out, and_8_out,
       and_9_out, and_10_out, and_11_out, and_12_out, and_13_out, and_14_out, and_15_out, and_16_out,
       and_17_out, and_18_out, and_19_out, and_21_out, and_22_out, and_24_out, and_26_out, and_27_out,
       button_1_out, button_2_out, button_3_out, Byte, Clk, clock_1_out, demultiplexer_1_out0,
       demultiplexer_1_out1, demultiplexer_1_out2, demultiplexer_1_out3, demultiplexer_1_out4,
       demultiplexer_1_out5, demultiplexer_1_out6, demultiplexer_1_out7, demultiplexer_1_out8,
       demultiplexer_1_out9, demultiplexer_1_out10, demultiplexer_1_out11, demultiplexer_1_out12,
       demultiplexer_1_out13, demultiplexer_1_out14, demultiplexer_1_out15, Exec, F, H, Int, j_k_ff_1_q,
       j_k_ff_1_qn, Jump, Latch, LatchF, Load, not_1_out, not_2_out, not_3_out, not_4_out, not_6_out,
       or_1_out, or_2_out, or_3_out, or_5_out, or_8_out, Reset, RW, Stack, Word, xnor_1_out, xnor_2_out,
       xor_1_out, xor_2_out;
  wire [3:0] comparator_1_eq, Cond, CVNZ, multiplexer_14_out, Op2, Op4, undriven_4;
  wire [6:2] pla_1_out;
  wire [7:0] register_3_q, register_4_q, register_9_q, register_10_q, register_15_q, register_16_q,
       register_21_q, register_22_q, undriven_7, undriven_8, undriven_9, undriven_10;
  wire [11:0] undriven_5;
  wire [15:0] and_23_out, divider_1_out, divider_1_rem, multiplexer_12_out, multiplexer_13_out,
       multiplier_1_out, negator_1_out, not_5_out, or_9_out, r0_q, r1_q, ram_1_p1, register_2_q,
       register_5_q, register_7_q, register_8_q, register_11_q, register_13_q, register_14_q, register_17_q,
       register_18_q, register_20_q, shifter_1_out, shifter_2_out, undriven_2, undriven_3, undriven_6,
       xor_3_out;
  wire [23:0] Code24;
  wire [26:24] IR_q;
  wire [31:0] adder_1_out, adder_2_out, adder_3_out, Addr, Base, Const8, Data, Din, Dout, f0_q, f1_q, f2_q,
       f3_q, fp_q, lr_q, multiplexer_2_out, multiplexer_3_out, multiplexer_4_out, multiplexer_8_out,
       multiplexer_9_out, multiplexer_10_out, Offset, Offset24, PC, Primary, SP, undriven;
  wire [31:8] multiplexer_5_out, multiplexer_6_out, multiplexer_7_out;

  Multiplexer #(.select(4)) multiplexer_1 (
    .in0(1'b0), .in1(CVNZ[0]), .in2(not_1_out), .in3(CVNZ[1]), .in4(not_2_out), .in5(CVNZ[2]),
    .in6(not_3_out), .in7(CVNZ[3]), .in8(not_4_out), .in9(and_1_out), .in10(or_1_out), .in11(xor_1_out),
    .in12(xnor_1_out), .in13(or_2_out), .in14(and_6_out), .in15(1'b1), .out(Exec), .sel(Cond));
  not not_1 (not_1_out, CVNZ[0]);
  not not_2 (not_2_out, CVNZ[1]);
  not not_3 (not_3_out, CVNZ[2]);
  Demultiplexer #(.select(4)) demultiplexer_1 (
    .out0(demultiplexer_1_out0), .out1(demultiplexer_1_out1), .out2(demultiplexer_1_out2),
    .out3(demultiplexer_1_out3), .out4(demultiplexer_1_out4), .out5(demultiplexer_1_out5),
    .out6(demultiplexer_1_out6), .out7(demultiplexer_1_out7), .out8(demultiplexer_1_out8),
    .out9(demultiplexer_1_out9), .out10(demultiplexer_1_out10), .out11(demultiplexer_1_out11),
    .out12(demultiplexer_1_out12), .out13(demultiplexer_1_out13), .out14(demultiplexer_1_out14),
    .out15(demultiplexer_1_out15), .in(Latch), .sel(Code24[3:0]));
  not not_4 (not_4_out, CVNZ[3]);
  and and_1 (and_1_out, ~CVNZ[0], CVNZ[3]);  // AND_Gate
  or or_1 (or_1_out, CVNZ[0], ~CVNZ[3]);  // OR_Gate
  and and_2 (and_2_out, Code24[23], demultiplexer_1_out0);
  and and_3 (and_3_out, H, demultiplexer_1_out0);
  and and_4 (and_4_out, Code24[23], demultiplexer_1_out1);
  and and_5 (and_5_out, H, demultiplexer_1_out1);
  xor xor_1 (xor_1_out, CVNZ[1], CVNZ[2]);
  xnor xnor_1 (xnor_1_out, CVNZ[1], CVNZ[2]);
  Register #(.trigger("falling"), .width(16)) r0 (
    .D(undriven[31:16]), .en(and_2_out), .clk(Clk), .Q(r0_q), .clr(Reset));
  Register #(.trigger("falling")) register_1 (
    .D(undriven[15:8]), .en(and_3_out), .clk(Clk), .Q(register_2_q[15:8]), .clr(Reset));
  Register #(.trigger("falling")) register_2 (
    .D(undriven[7:0]), .en(demultiplexer_1_out0), .clk(Clk), .Q(register_2_q[7:0]), .clr(Reset));
  Register #(.trigger("falling"), .width(16)) r1 (
    .D(undriven[31:16]), .en(and_4_out), .clk(Clk), .Q(r1_q), .clr(Reset));
  Register #(.trigger("falling")) register_3 (
    .D(undriven[15:8]), .en(and_5_out), .clk(Clk), .Q(register_3_q), .clr(Reset));
  Register #(.trigger("falling")) register_4 (
    .D(undriven[7:0]), .en(demultiplexer_1_out1), .clk(Clk), .Q(register_4_q), .clr(Reset));
  xor xor_2 (xor_2_out, CVNZ[1], CVNZ[2]);
  or or_2 (or_2_out, CVNZ[0], xor_2_out);
  xnor xnor_2 (xnor_2_out, CVNZ[1], CVNZ[2]);
  and and_6 (and_6_out, ~CVNZ[0], xnor_2_out);  // AND_Gate
  and and_7 (and_7_out, Code24[23], demultiplexer_1_out2);
  and and_8 (and_8_out, Code24[23], demultiplexer_1_out2);
  and and_9 (and_9_out, Code24[23], demultiplexer_1_out3);
  and and_10 (and_10_out, Code24[23], demultiplexer_1_out3);
  Register #(.trigger("falling"), .width(16)) register_5 (
    .D(undriven[31:16]), .en(and_7_out), .clk(Clk), .Q(register_5_q), .clr(Reset));
  Register #(.trigger("falling")) register_6 (
    .D(undriven[15:8]), .en(and_8_out), .clk(Clk), .Q(register_7_q[15:8]), .clr(Reset));
  Register #(.trigger("falling")) register_7 (
    .D(undriven[7:0]), .en(demultiplexer_1_out2), .clk(Clk), .Q(register_7_q[7:0]), .clr(Reset));
  Register #(.trigger("falling"), .width(16)) register_8 (
    .D(undriven[31:16]), .en(and_9_out), .clk(Clk), .Q(register_8_q), .clr(Reset));
  Register #(.trigger("falling")) register_9 (
    .D(undriven[15:8]), .en(and_10_out), .clk(Clk), .Q(register_9_q), .clr(Reset));
  Register #(.trigger("falling")) register_10 (
    .D(undriven[7:0]), .en(demultiplexer_1_out3), .clk(Clk), .Q(register_10_q), .clr(Reset));
  and and_11 (and_11_out, Code24[23], demultiplexer_1_out4);
  and and_12 (and_12_out, H, demultiplexer_1_out4);
  and and_13 (and_13_out, Code24[23], demultiplexer_1_out5);
  and and_14 (and_14_out, H, demultiplexer_1_out5);
  Register #(.trigger("falling"), .width(16)) register_11 (
    .D(undriven[31:16]), .en(and_11_out), .clk(Clk), .Q(register_11_q), .clr(Reset));
  Register #(.trigger("falling")) register_12 (
    .D(undriven[15:8]), .en(and_12_out), .clk(Clk), .Q(register_13_q[15:8]), .clr(Reset));
  Register #(.trigger("falling")) register_13 (
    .D(undriven[7:0]), .en(demultiplexer_1_out4), .clk(Clk), .Q(register_13_q[7:0]), .clr(Reset));
  Register #(.trigger("falling"), .width(16)) register_14 (
    .D(undriven[31:16]), .en(and_13_out), .clk(Clk), .Q(register_14_q), .clr(Reset));
  Register #(.trigger("falling")) register_15 (
    .D(undriven[15:8]), .en(and_14_out), .clk(Clk), .Q(register_15_q), .clr(Reset));
  Register #(.trigger("falling")) register_16 (
    .D(undriven[7:0]), .en(demultiplexer_1_out5), .clk(Clk), .Q(register_16_q), .clr(Reset));
  Register #(.trigger("falling"), .width(16)) register_17 (
    .D(undriven[31:16]), .en(and_15_out), .clk(Clk), .Q(register_17_q), .clr(Reset));
  and and_15 (and_15_out, Code24[23], demultiplexer_1_out6);
  and and_16 (and_16_out, H, demultiplexer_1_out6);
  Register #(.trigger("falling"), .width(16)) register_18 (
    .D(undriven[31:16]), .en(and_17_out), .clk(Clk), .Q(register_18_q), .clr(Reset));
  and and_17 (and_17_out, Code24[23], demultiplexer_1_out7);
  and and_18 (and_18_out, H, demultiplexer_1_out7);
  Register #(.trigger("falling")) register_19 (
    .D(undriven[15:8]), .en(and_16_out), .clk(Clk), .Q(register_20_q[15:8]), .clr(Reset));
  Register #(.trigger("falling")) register_20 (
    .D(undriven[7:0]), .en(demultiplexer_1_out6), .clk(Clk), .Q(register_20_q[7:0]), .clr(Reset));
  Register #(.trigger("falling")) register_21 (
    .D(undriven[15:8]), .en(and_18_out), .clk(Clk), .Q(register_21_q), .clr(Reset));
  Register #(.trigger("falling")) register_22 (
    .D(undriven[7:0]), .en(demultiplexer_1_out7), .clk(Clk), .Q(register_22_q), .clr(Reset));
  Multiplexer #(.width(32)) multiplexer_2 (
    .in0(adder_1_out), .in1(Data), .out(multiplexer_2_out), .sel(demultiplexer_1_out14));
  or or_3 (or_3_out, demultiplexer_1_out14, Stack);
  Multiplexer #(.width(32)) multiplexer_3 (
    .in0(adder_2_out), .in1(Data), .out(multiplexer_3_out), .sel(demultiplexer_1_out15));
  Register #(.trigger("falling"), .width(32)) f0 (
    .D(Data), .en(demultiplexer_1_out8), .clk(Clk), .Q(f0_q), .clr(Reset));
  Register #(.trigger("falling"), .width(32)) f1 (
    .D(Data), .en(demultiplexer_1_out9), .clk(Clk), .Q(f1_q), .clr(Reset));
  Register #(.trigger("falling"), .width(32)) f2 (
    .D(Data), .en(demultiplexer_1_out10), .clk(Clk), .Q(f2_q), .clr(Reset));
  Register #(.trigger("falling"), .width(32)) f3 (
    .D(Data), .en(demultiplexer_1_out11), .clk(Clk), .Q(f3_q), .clr(Reset));
  Register #(.trigger("falling"), .width(32)) lr (
    .D(Data), .en(demultiplexer_1_out12), .clk(Clk), .Q(lr_q), .clr(Reset));
  Register #(.trigger("falling"), .width(32)) fp (
    .D(Data), .en(demultiplexer_1_out13), .clk(Clk), .Q(fp_q), .clr(Reset));
  Register #(.trigger("falling"), .width(32)) u_SP (
    .D(multiplexer_2_out), .en(or_3_out), .clk(Clk), .Q(SP), .clr(Reset));
  Register #(.trigger("falling"), .width(32)) u_PC (.D(multiplexer_3_out), .en(1'b1), .clk(Clk), .Q(PC), .clr(Reset));
  Adder #(.width(32)) adder_1 (.a(SP), .b(Const8), .out(adder_1_out));  // open: cin, cout
  Multiplexer #(.width(32)) multiplexer_4 (.in0(32'h4), .in1(Offset24), .out(multiplexer_4_out), .sel(Jump));
  Multiplexer #(.select(4), .width(32)) multiplexer_5 (
    .in0({r0_q, register_2_q}), .in1({r1_q, register_3_q, register_4_q}), .in2({register_5_q, register_7_q}),
    .in3({register_8_q, register_9_q, register_10_q}), .in4({register_11_q, register_13_q}),
    .in5({register_14_q, register_15_q, register_16_q}), .in6({register_17_q, register_20_q}),
    .in7({register_18_q, register_21_q, register_22_q}), .in8(f0_q), .in9(f1_q), .in10(f2_q), .in11(f3_q),
    .in12(lr_q), .in13(fp_q), .in14(SP), .in15(PC), .out({multiplexer_5_out, Primary[7:0]}), .sel(Code24[3:0]));
  Multiplexer #(.select(4), .width(32)) multiplexer_6 (
    .in0({r0_q, register_2_q}), .in1({r1_q, register_3_q, register_4_q}), .in2({register_5_q, register_7_q}),
    .in3({register_8_q, register_9_q, register_10_q}), .in4({register_11_q, register_13_q}),
    .in5({register_14_q, register_15_q, register_16_q}), .in6({register_17_q, register_20_q}),
    .in7({register_18_q, register_21_q, register_22_q}), .in8(f0_q), .in9(f1_q), .in10(f2_q), .in11(f3_q),
    .in12(lr_q), .in13(fp_q), .in14(SP), .in15(PC), .out({multiplexer_6_out, Base[7:0]}), .sel(Code24[7:4]));
  Multiplexer #(.select(4), .width(32)) multiplexer_7 (
    .in0({r0_q, register_2_q}), .in1({r1_q, register_3_q, register_4_q}), .in2({register_5_q, register_7_q}),
    .in3({register_8_q, register_9_q, register_10_q}), .in4({register_11_q, register_13_q}),
    .in5({register_14_q, register_15_q, register_16_q}), .in6({register_17_q, register_20_q}),
    .in7({register_18_q, register_21_q, register_22_q}), .in8(f0_q), .in9(f1_q), .in10(f2_q), .in11(f3_q),
    .in12(lr_q), .in13(fp_q), .in14(SP), .in15(PC), .out({multiplexer_7_out, Offset[7:0]}), .sel(Code24[11:8]));
  Adder #(.width(32)) adder_2 (.a(PC), .b(multiplexer_4_out), .out(adder_2_out));  // open: cin, cout
  assign Primary[15:8] = H ? multiplexer_5_out[15:8] : 8'bz;  // Controlled_Buffer controlled_buffer_1
  assign Primary[31:16] = Code24[23] ? multiplexer_5_out[31:16] : 16'bz;  // Controlled_Buffer controlled_buffer_2
  assign Base[15:8] = H ? multiplexer_6_out[15:8] : 8'bz;  // Controlled_Buffer controlled_buffer_3
  assign Base[31:16] = Code24[23] ? multiplexer_6_out[31:16] : 16'bz;  // Controlled_Buffer controlled_buffer_4
  assign Offset[15:8] = H ? multiplexer_7_out[15:8] : 8'bz;  // Controlled_Buffer controlled_buffer_5
  assign Offset[31:16] = Code24[23] ? multiplexer_7_out[31:16] : 16'bz;  // Controlled_Buffer controlled_buffer_6
  Multiplexer #(.width(32)) multiplexer_8 (.in0(Offset), .in1(Const8), .out(multiplexer_8_out), .sel(Code24[21]));
  assign Data = and_19_out ? multiplexer_8_out : 32'bz;  // Controlled_Buffer controlled_buffer_7
  and and_19 (and_19_out, ALU, Clk);
  Button button_1 (.out(button_1_out));
  or or_4 (Reset, button_1_out, button_2_out);
  Button button_2 (.out(button_2_out));
  Adder #(.width(32)) adder_3 (.a(Base), .b(multiplexer_9_out), .out(adder_3_out));  // open: cin, cout
  Multiplexer #(.width(32)) multiplexer_9 (.in0(Offset), .in1(Const8), .out(multiplexer_9_out), .sel(Code24[21]));
  assign Data = or_5_out ? Din : 32'bz;  // Controlled_Buffer controlled_buffer_8
  or or_5 (or_5_out, ~Clk, or_8_out);  // OR_Gate
  or or_6 (Latch, or_8_out, ALU);
  // AND_Gate and_20 is placed but not wired
  or or_7 (Clk, clock_1_out, button_3_out);
  Clock clock_1 (.out(clock_1_out));
  Button button_3 (.out(button_3_out));
  Multiplexer #(.width(32)) multiplexer_10 (.in0(adder_3_out), .in1(SP), .out(multiplexer_10_out), .sel(Stack));
  assign Dout = RW ? Primary : 32'bz;  // Controlled_Buffer controlled_buffer_9
  and and_21 (and_21_out, Load, ~Code24[20]);  // AND_Gate
  or or_8 (or_8_out, and_21_out, and_22_out);
  and and_22 (and_22_out, Word, j_k_ff_1_q);
  Negator #(.width(16)) negator_1 (.in({undriven_5, undriven_4}), .out(negator_1_out));
  Multiplier #(.width(16)) multiplier_1 (
    .a(ram_1_p1), .b({undriven_5, undriven_4}), .out(multiplier_1_out));  // open: cin, cout
  Divider #(.width(16)) divider_1 (
    .a(ram_1_p1), .b({undriven_5, undriven_4}), .out(divider_1_out), .rem(divider_1_rem));  // open: upper
  assign not_5_out = ~ram_1_p1;  // NOT_Gate not_5, 16 bits wide
  assign and_23_out = ram_1_p1 & {undriven_5, undriven_4};  // AND_Gate and_23, 16 bits wide
  assign or_9_out = ram_1_p1 | {undriven_5, undriven_4};  // OR_Gate or_9, 16 bits wide
  assign xor_3_out = ram_1_p1 ^ {undriven_5, undriven_4};  // XOR_Gate xor_3, 16 bits wide
  Shifter #(.shift("lr"), .width(16)) shifter_1 (.in(ram_1_p1), .\dist (undriven_4), .out(shifter_1_out));
  Shifter #(.width(16)) shifter_2 (.in(ram_1_p1), .\dist (undriven_4), .out(shifter_2_out));
  Multiplexer #(.width(32)) multiplexer_11 (.in0(PC), .in1(multiplexer_10_out), .out(Addr), .sel(and_24_out));
  and and_24 (and_24_out, Clk, j_k_ff_1_qn, Load);
  and and_25 (RW, Clk, Load, Code24[20]);
  J_K_Flip_Flop #(.trigger("falling")) j_k_ff_1 (
    .J(Word), .K(Word), .clk(Clk), .Q(j_k_ff_1_q), .Qn(j_k_ff_1_qn), .reset(Reset));  // open: preset
  Multiplexer #(.width(16)) multiplexer_12 (
    .in0(undriven_3), .in1(negator_1_out), .out(multiplexer_12_out), .sel(and_26_out));
  and and_26 (and_26_out, multiplexer_14_out[1], ~multiplexer_14_out[2], ~multiplexer_14_out[3]);  // AND_Gate
  // RAM #(.addrWidth(24), .enables("line"), .line("quad"), .misaligned("true"), .trigger("falling")) ram_1: pin names not known; wires that end beside it: ram_1_p1, Addr[23:0], RW, RW, H, Code24[21], Clk
  Register #(.width(32)) IR (.D(Data), .en(j_k_ff_1_qn), .clk(Clk), .Q({Cond, F, IR_q, Code24}), .clr(Reset));
  PLA #(.in_width(4), .out_width(8), .\table ("0xxx 00000000\n1000 00000001\n1001 00000010\n1010 00000000\n1011 00001000\n1100 00011000\n1101 00100000\n1110 01000000\n1111 11000000")) pla_1 (
    .in({Exec, IR_q}), .out({Word, pla_1_out[6], Int, Stack, Load, pla_1_out[2], ALU, Jump}));
  Controlled_Buffer #(.width(16)) controlled_buffer_10 (.in(multiplexer_13_out), .en(and_27_out));  // open: out
  Multiplexer #(.select(4), .width(16)) multiplexer_13 (
    .in0(undriven_2), .in1(undriven_6), .in2(undriven_6), .in3(undriven_6), .in4(multiplier_1_out),
    .in5(not_5_out), .in6(divider_1_out), .in7(divider_1_rem), .in8(and_23_out), .in9(or_9_out),
    .in10(xor_3_out), .in13(negator_1_out), .in14(shifter_1_out), .in15(shifter_2_out),
    .out(multiplexer_13_out), .sel(multiplexer_14_out));  // open: in11, in12
  buf and_27 (and_27_out, ALU);  // AND_Gate
  Multiplexer #(.width(4)) multiplexer_14 (.in0(Op4), .in1(Op2), .out(multiplexer_14_out), .sel(Byte));
  assign Offset24 = {{8{Code24[23]}}, Code24};  // Bit_Extender bit_extender_1
  Comparator #(.width(16)) comparator_1 (
    .a(multiplexer_13_out), .b({16{1'b0}}), .eq(comparator_1_eq[0]), .lt(comparator_1_eq[1]));  // open: gt
  and and_28 (LatchF, multiplexer_14_out[0], multiplexer_14_out[1], ~multiplexer_14_out[2], ~multiplexer_14_out[3], ALU);  // AND_Gate
  or or_10 (H, Code24[23], Code24[22]);
  Register #(.trigger("falling"), .width(4)) Flag (.D(comparator_1_eq), .en(LatchF), .clk(Clk), .Q(CVNZ), .clr(Reset));
  not not_6 (not_6_out, RW);
  assign Din = not_6_out ? {undriven_10, undriven_9, undriven_8, undriven_7} : 32'bz;  // Controlled_Buffer controlled_buffer_11
  assign Const8 = {{24{Code24[15]}}, Code24[15:8]};  // Bit_Extender bit_extender_2

  // Other names for the same wires on the sheet: Rd[3:0] = Code24[3:0]; Rs[3:0] = Code24[7:4]; I = Code24[21];
  //   W = Code24[23]; Rs2[3:0] = Code24[11:8]; Op5[4:0] = Code24[20:16]; D = Code24[20]
endmodule

module MyAdder (
  input  [31:0] A,
  input  [31:0] B,
  input  Cin,
  input  H,
  input  W,
  output [31:0] Add,
  output V,
  output Cout
);

  wire adder_1_cout, adder_2_cout, adder_3_cout, adder_4_cout, adder_5_cout, adder_6_cout, xor_1_out,
       xor_2_out, xor_3_out;

  Adder #(.width(7)) adder_1 (.a(A[6:0]), .b(B[6:0]), .out(Add[6:0]), .cin(Cin), .cout(adder_1_cout));
  Adder #(.width(1)) adder_2 (.a(A[7]), .b(B[7]), .out(Add[7]), .cin(adder_1_cout), .cout(adder_2_cout));
  Adder #(.width(7)) adder_3 (.a(A[14:8]), .b(B[14:8]), .out(Add[14:8]), .cin(adder_2_cout), .cout(adder_3_cout));
  Adder #(.width(1)) adder_4 (.a(A[15]), .b(B[15]), .out(Add[15]), .cin(adder_3_cout), .cout(adder_4_cout));
  Adder #(.width(15)) adder_5 (.a(A[30:16]), .b(B[30:16]), .out(Add[30:16]), .cin(adder_4_cout), .cout(adder_5_cout));
  Adder #(.width(1)) adder_6 (.a(A[31]), .b(B[31]), .out(Add[31]), .cin(adder_5_cout), .cout(adder_6_cout));
  xor xor_1 (xor_1_out, adder_6_cout, adder_5_cout);
  Multiplexer #(.select(2)) multiplexer_1 (
    .in0(adder_2_cout), .in1(adder_4_cout), .in2(adder_6_cout), .in3(adder_6_cout), .out(Cout), .sel({W, H}));
  xor xor_2 (xor_2_out, adder_2_cout, adder_1_cout);
  xor xor_3 (xor_3_out, adder_4_cout, adder_3_cout);
  Multiplexer #(.select(2)) multiplexer_2 (
    .in0(xor_2_out), .in1(xor_3_out), .in2(xor_1_out), .in3(xor_1_out), .out(V), .sel({W, H}));
endmodule
